# Fritzing sketch Robonaut (saved by Fritzing 0.9.2b)
breadboards: 1

parts:
  M1 = DC Motor
  Part1 = Arduino Mega 2560 (Rev3)
  J1 = Infrared Proximity Sensor
  J2 = Infrared Proximity Sensor
  J3 = Infrared Proximity Sensor
  J4 = Infrared Proximity Sensor
  J5 = Infrared Proximity Sensor
  MD03A1 = Dual VNH2SP30 Motor Driver [part_number=MD03A]
  M2 = DC Motor
  R1 = Photocell (LDR) [package=THT]
  R3 = Photocell (LDR) [package=THT]
  R4 = Resistor [tolerance=±5% resistance=1k package=THT]
  R5 = Resistor [tolerance=±5% resistance=1k package=THT]
  R6 = Resistor [tolerance=±5% resistance=1k package=THT]
  R7 = PHOTOCELL [package=photocell]

nets:
  N1: M1.pin_1, MD03A1.OUT_1B
  N2: M1.pin_2, MD03A1.OUT_1A
  N3: Part1.A0, R1.pin_0, R4.Pin_1
  N4: Part1.A1, R5.Pin_0, R7.P$2
  N5: Part1.A2, R3.pin_1, R6.Pin_0
  N6: Part1.D19/RX1, J3.Vout
  N7: Part1.D18/TX1, J1.Vout
  N8: Part1.D17_PWM/RX2, J2.Vout
  N9: Part1.D16_PWM/TX2, J4.Vout
  N10: Part1.D15/RX3, J5.Vout
  N11: Part1.D13_PWM, MD03A1.2INb#143
  N12: Part1.D12_PWM, MD03A1.2INb#142
  N13: Part1.D11_PWM, MD03A1.2PWM
  N14: Part1.D10_PWM, MD03A1.1INa
  N15: Part1.D9_PWM, MD03A1.1INb
  N16: Part1.D8_PWM, MD03A1.PWM
  5V: Part1.5V, J3.Vcc, R1.pin_1, R3.pin_0, R7.P$1
  GND: Part1.GND, J3.GND, MD03A1.GND, R4.Pin_0, R5.Pin_1, R6.Pin_1
  VIN: Part1.VIN, MD03A1.VIN
  N17: MD03A1.OUT_2A, M2.pin_2
  N18: MD03A1.OUT_2B, M2.pin_1
